# Fritzing sketch FinalFritzing (saved by Fritzing 0.9.3b)
breadboards: 2

parts:
  U1 = ESP8266 WiFi Module [part_number=ESP8266]  # not connected
  Part1 = RFID USB Reader
  Raspberry_Pi_1 = Raspberry Pi 3 [part_number=RPI-3-V1.2]
  RHT1 = Humidity and Temperature Sensor RHT03
  R1 = Resistor [tolerance=±10% resistance=10k package=THT]
  IC1 = L293D [package=THT]
  M1 = DC Motor
  VCC1 = Battery
  LED1 = smd LED [color="Red (633nm)" package="0603 [SMD]"]
  R2 = Resistor [tolerance=±5% resistance=220k package=THT]
  R3 = Photocell (LDR) [package=THT]
  R4 = Resistor [tolerance=±5% resistance=10k package="0603 [SMD]"]

nets:
  N1: Part1.GNDT, Part1.CP, R3.pin_0
  N2: Part1.ANT2, R4.Pin_1
  N3: Raspberry_Pi_1.GIPO17, R2.Pin_0
  N4: Raspberry_Pi_1.GIPO22, IC1.Enable_1
  N5: Raspberry_Pi_1.GND, RHT1.GND_2, LED1.cathode
  N6: Raspberry_Pi_1.GIPO7, IC1.0V, VCC1.-
  N7: Raspberry_Pi_1.GIPO24, RHT1.Vcc, R1.Pin_0, R1.Pin_1
  N8: Raspberry_Pi_1.GIPO23, IC1.In_1
  N9: Raspberry_Pi_1.GIPO18, RHT1.Data-signal
  N10: IC1.Out_1_(_Controlled_by_Enable_1_), M1.pin_2
  N11: IC1.Out_2_(_Controlled_by_Enable_1_), M1.pin_1
  N12: IC1.+Vmotor, IC1.+V, VCC1.+
  N13: LED1.anode, R2.Pin_1
  N14: R3.pin_1, R4.Pin_0

notes:
  RFID READER
  (left to right)
  Orange: VCC (rfid) / 3.3 V (ESP 8266)
  Yellow: RST (rfid) / D0 (ESP 8266)
  Black: GND / GND
  Green: MISO (rfid) / D6 (ESP 8266)
  White: MOSI (rfid) / D7 (ESP 8266)
  Grey: SCK (rfid) / D5 (ESP 8266)
  Orange: SS/SDA (rfid) / D8 (ESP 8266)
  3v3
  A0
  GND
  LED RES 220k ohms
  LDR RES 10k ohms
  GPIO17
  GPIO23
  GPIO7
  GPIO22
  DHT 11 RES 10k ohms
  GPIO18
  GPIO24
