# Fritzing sketch phase2 (saved by Fritzing 0.9.3b)
breadboards: 1

parts:
  Raspberry_Pi_1 = Raspberry Pi 3 [part_number=RPI-3-V1.2]
  RHT1 = Humidity and Temperature Sensor RHT03
  IC1 = L293D [package=THT]
  VCC2 = Battery
  M1 = DC Motor
  R1 = Resistor [tolerance=±5% resistance=10k package=THT]

nets:
  N1: Raspberry_Pi_1.GND, Raspberry_Pi_1.GIPO7, Raspberry_Pi_1.GIPO15, RHT1.GND_2, IC1.0V, VCC2.-
  N2: Raspberry_Pi_1.GIPO17, Raspberry_Pi_1.GIPO18, RHT1.Data-signal
  N3: Raspberry_Pi_1.GIPO22, IC1.Enable_1
  3V3: Raspberry_Pi_1.3V3, Raspberry_Pi_1.GIPO24, RHT1.Vcc, R1.Pin_0, R1.Pin_1
  N4: Raspberry_Pi_1.GIPO12, IC1.In_2
  N5: Raspberry_Pi_1.GIPO23, IC1.In_1
  N6: IC1.Out_2_(_Controlled_by_Enable_1_), M1.pin_1
  N7: IC1.+Vmotor, IC1.+V, VCC2.+
