# Fritzing sketch phase3 (saved by Fritzing 0.9.3b)
breadboards: 1

parts:
  Raspberry_Pi_1 = Raspberry Pi 3 [part_number=RPI-3-V1.2]
  LED1 = smd LED [color="Red (633nm)" package="0603 [SMD]"]
  R1 = Resistor [tolerance=±5% resistance=10k package="2512 [SMD]"]
  R2 = Photocell (LDR) [package=THT]
  U1 = ESP8266 WiFi Module [part_number=ESP8266]
  R3 = Resistor [tolerance=±5% resistance=220 package="2512 [SMD]"]

nets:
  N1: Raspberry_Pi_1.GND, LED1.cathode
  N2: Raspberry_Pi_1.GPIO23, R3.Pin_0
  N3: LED1.anode, R3.Pin_1
  N4: R1.Pin_0, R2.pin_1, U1.ADC_0
  N5: R1.Pin_1, U1.GND
  N6: R2.pin_0, U1.VCC

notes:
  GROUND
  GPIO23
  LED RES 220k ohms
  LDR RES 10k ohms
  A0
  GRND
  3v3
